# Fritzing sketch raPID_FC_mini (saved by Fritzing 0.9.3b)
circuit board: 6.00218cm x 3.00427cm
breadboards: 1

parts:
  S_+_- = Basic Servo
  Teensy_3_2 = Teensy 3.1
  MPU-6050 = MPU-6050 Board GY-521 [form="♀ (female)" package=THT]
  J2 = Basic Servo
  J3 = Basic Servo
  OUTPUT = Basic Servo
  INPUT_SIGNAL = Header 6 [package=molex-1x6-ra]
  LED = LED - 3mm [color="Red (633nm)" package="3 mm [THT]"]
  DBG = LED - 3mm [color="Red (633nm)" package="3 mm [THT]"]

nets:
  GND: S_+_-.gnd, Teensy_3_2.GND, MPU-6050.pin2, J2.gnd, J3.gnd, OUTPUT.gnd, LED.cathode
  VCC: S_+_-.vcc, Teensy_3_2.Vin
  N1: S_+_-.pulse, Teensy_3_2.D3
  N2: Teensy_3_2.D4, OUTPUT.pulse
  N3: Teensy_3_2.D5, J2.pulse
  N4: Teensy_3_2.D6, J3.pulse
  N5: Teensy_3_2.D7, INPUT_SIGNAL.6
  N6: Teensy_3_2.D8, INPUT_SIGNAL.5
  N7: Teensy_3_2.D9, INPUT_SIGNAL.4
  N8: Teensy_3_2.D10, INPUT_SIGNAL.3
  N9: Teensy_3_2.D11, INPUT_SIGNAL.2
  N10: Teensy_3_2.D12, INPUT_SIGNAL.1
  N11: Teensy_3_2.D13, MPU-6050.pin8
  N12: Teensy_3_2.A4/D18, MPU-6050.pin4
  N13: Teensy_3_2.A5/D19, MPU-6050.pin3
  N14: Teensy_3_2.A6/D20, LED.anode
  N15: Teensy_3_2.A9/D23, DBG.cathode
  N16: Teensy_3_2.3V3, MPU-6050.pin1

custom parts:
  MPU-6050 Board GY-521: Acelerometro y Giroscopio MPU-6050 Board GY-521
